# Fritzing sketch Circut2 (saved by Fritzing 0.9.3b)
circuit board: 10.2688cm x 9.61876cm
stripboards: 1

parts:
  Arduino = Arduino Mega 2560 (Rev3)
  TouchRes4 = Resistor [tolerance=±5% resistance=10M package=THT]
  TouchRes3 = Resistor [tolerance=±5% resistance=10M package=THT]
  TouchRes2 = Resistor [tolerance=±5% resistance=10M package=THT]
  TouchRes1 = Resistor [tolerance=±5% resistance=10M package=THT]
  Touch1 = CAPSENSE_PAD [part_number=1 package=capsense_pad]
  Touch2 = CAPSENSE_PAD [part_number=2 package=capsense_pad]
  Touch3 = CAPSENSE_PAD [part_number=3 package=capsense_pad]
  Touch4 = CAPSENSE_PAD [part_number=4 package=capsense_pad]
  LED1 = Apa102c
  LED4 = Apa102c
  LED2 = Apa102c
  LED3 = Apa102c
  LCD_Screen = LCD-16X2 [package=lcd-8x2]
  LCDContrastRes = Resistor [tolerance=±5% resistance=220 package=THT]
  Touchcap4 = Ceramic Capacitor [capacitance=100pF package="100 mil [THT, multilayer]"]
  Touchcap3 = Ceramic Capacitor [capacitance=100pF package="100 mil [THT, multilayer]"]
  Touchcap2 = Ceramic Capacitor [capacitance=100pF package="100 mil [THT, multilayer]"]
  Touchcap1 = Ceramic Capacitor [capacitance=100pF package="100 mil [THT, multilayer]"]
  Hcontrol = Rotary Potentiometer (Small) [maximum_resistance=10kΩ package=THT]
  Rcontrol = Rotary Potentiometer (Small) [maximum_resistance=10kΩ package=THT]
  Tbutton = Pushbutton [package="[THT]"]
  Reset_Button = Pushbutton [package="[THT]"]

nets:
  N1: Arduino.A0, Rcontrol.wiper
  N2: Arduino.A1, Hcontrol.wiper
  N3: Arduino.D12_PWM, TouchRes4.Pin_0, Touch4.RECEIVE, Touchcap4.1
  N4: Arduino.D11_PWM, TouchRes3.Pin_0, Touch3.RECEIVE, Touchcap3.1
  N5: Arduino.D10_PWM, Arduino.D9_PWM, TouchRes2.Pin_0, TouchRes1.Pin_0, Touch1.RECEIVE, Touch2.RECEIVE, Touchcap2.1, Touchcap1.1
  N6: Arduino.D8_PWM, TouchRes4.Pin_1, TouchRes3.Pin_1, TouchRes2.Pin_1, TouchRes1.Pin_1
  5V: Arduino.IOREF, Arduino.5V, LED4.V+, LCD_Screen.VDD, LCD_Screen.A, LCDContrastRes.Pin_0, Hcontrol.leg1, Rcontrol.leg1
  N7: Arduino.RESET, Reset_Button.Pin_3, Reset_Button.Pin_4
  GND: Arduino.GND, LED1.V-, LED4.Cl-, LED4.D-, LCD_Screen.VSS, LCD_Screen.K, Touchcap4.0, Touchcap3.0, Touchcap2.0, Touchcap1.0, Hcontrol.leg2, Rcontrol.leg2, Tbutton.Pin_2, Reset_Button.Pin_1, Reset_Button.Pin_2
  N8: Arduino.D2_PWM, LED1.D+
  N9: Arduino.D3_PWM, LED1.Cl+
  N10: Arduino.D4_PWM, Tbutton.Pin_3, Tbutton.Pin_4
  N11: LED1.Cl-, LED2.Cl+
  N12: LED1.D-, LED2.D+
  N13: LED1.V+, LED2.V-
  N14: LED4.V-, LED3.V+
  N15: LED4.D+, LED3.D-
  N16: LED4.Cl+, LED3.Cl-
  N17: LED2.Cl-, LED3.Cl+
  N18: LED2.D-, LED3.D+
  N19: LED2.V+, LED3.V-
  N20: LCD_Screen.VO, LCDContrastRes.Pin_1

custom parts:
  Apa102c: A dummy, proxy, ersatz, stand-in part for whatever you want. With 6 pins on a 300mil inline pin header footprint.
